# Fritzing sketch Moodlamp (saved by Fritzing 0.9.1b)
circuit board: 4cm x 6cm
circuit board: 4cm x 6cm
perfboards: 1

parts:
  U3 = attiny85 [package=dip]
  U4 = Voltage Regulator - 5V [package="TO220 [THT]"]
  R18 = Resistor [tolerance=±5% resistance=10k package=THT]  # not connected
  R19 = Resistor [tolerance=±5% resistance=330 package=THT]
  R20 = Resistor [tolerance=±5% resistance=330 package=THT]
  R21 = Resistor [tolerance=±5% resistance=330 package=THT]
  VCC1 = Battery block 9V
  R22 = Rotary Potentiometer (Small) [maximum_resistance=100kΩ package=THT]
  S5 = Square Pushbutton
  U5 = SWITCH-SPST-2 [package=switch-spst-vertical]
  J1 = Screw terminal - 2 pins [package=THT]
  J2 = female pin header, 4 pins [form="♀ (female)"]
  J3 = female pin header, 3 pins [form="♀ (female)"]
  J4 = female pin header, 2 pins [form="♀ (female)"]
  J5 = female pin header, 4 pins [form="♀ (female)"]
  R23 = Resistor [tolerance=±5% resistance=330 package=THT]
  R24 = Resistor [tolerance=±5% resistance=330 package=THT]
  R25 = Resistor [tolerance=±5% resistance=330 package=THT]
  U7 = Voltage Regulator - 5V [package="TO220 [THT]"]
  J6 = Screw terminal - 2 pins [package=THT]
  R26 = Rotary Potentiometer (Small) [maximum_resistance=100kΩ package=THT]
  J7 = female pin header, 3 pins [form="♀ (female)"]
  J8 = female pin header, 2 pins [form="♀ (female)"]
  U6 = attiny85 [package=dip]
  R27 = Resistor [tolerance=±5% resistance=330 package=THT]
  S6 = Square Pushbutton

nets:
  N1: U3.Pin_2, S5.leg1
  N2: U3.Pin_3, R20.Pin_0
  N3: U3.Pin_5, R21.Pin_0
  N4: U3.Pin_6, R19.Pin_0
  N5: U3.Pin_7, R22.wiper, J3.pin2
  N6: U3.Pin_8, U4.output_voltage, R22.leg1, J3.pin1, J4.pin1
  N7: U4.input_voltage, VCC1.-, U5.O, J1.pin1
  N8: U4.GND, VCC1.+, R22.leg2, U5.P, J1.pin2, J2.pin2, J3.pin3
  N9: R19.Pin_1, J2.pin3
  N10: R20.Pin_1, J2.pin4
  N11: R21.Pin_1, J2.pin1
  N12: J5.pin1, R24.Pin_1
  N13: J5.pin2, R25.Pin_1
  N14: J5.pin3, U7.GND, J6.pin2, R26.leg2, J7.pin1, J8.pin1, U6.Pin_4, S6.leg1
  N15: J5.pin4, R23.Pin_0
  N16: U7.input_voltage, J6.pin1
  N17: U7.output_voltage, R26.leg1, J7.pin3, U6.Pin_8, R27.Pin_1
  N18: R26.wiper, J7.pin2, U6.Pin_7
  N19: J8.pin2, U6.Pin_2, R27.Pin_0, S6.leg0

notes:
  Striped = Jumper wires
  RGB Moodlamp
