# Fritzing sketch Moodlamp_Photocell (saved by Fritzing 0.9.1b)
circuit board: 4cm x 6cm
perfboards: 1

parts:
  J5 = female pin header, 4 pins [form="♀ (female)"]
  R1 = Resistor [tolerance=±5% resistance=330 package=THT]
  R2 = Resistor [tolerance=±5% resistance=330 package=THT]
  R3 = Resistor [tolerance=±5% resistance=330 package=THT]
  U7 = Voltage Regulator - 5V [package="TO220 [THT]"]
  J6 = Screw terminal - 2 pins [package=THT]
  R26 = Rotary Potentiometer (Small) [maximum_resistance=100kΩ package=THT]
  J7 = female pin header, 3 pins [form="♀ (female)"]
  J8 = female pin header, 2 pins [form="♀ (female)"]
  IC = attiny85 [package=dip]
  R4 = Resistor [tolerance=±5% resistance=330 package=THT]
  S6 = Square Pushbutton
  R5 = Resistor [tolerance=±5% resistance=330 package=THT]
  J9 = female pin header, 2 pins [form="♀ (female)"]

nets:
  N1: J5.pin1, R2.Pin_1
  N2: J5.pin2, R3.Pin_1
  N3: J5.pin3, U7.GND, J6.pin2, R26.leg2, J7.pin1, J8.pin1, IC.Pin_4, S6.leg1, J9.pin2
  N4: J5.pin4, R1.Pin_0
  N5: R1.Pin_1, IC.Pin_3
  N6: R2.Pin_0, IC.Pin_5
  N7: U7.input_voltage, J6.pin1
  N8: U7.output_voltage, R26.leg1, J7.pin3, IC.Pin_8, R4.Pin_1
  N9: R26.wiper, J7.pin2, IC.Pin_7
  N10: J8.pin2, IC.Pin_2, R4.Pin_0, S6.leg0, R5.Pin_1
  N11: R5.Pin_0, J9.pin1

notes:
  Striped = Jumper wires
  RGB Moodlamp
  David Thornton
  v1.0
